# Fritzing sketch Garaginator9000000 (saved by Fritzing 0.9.3b)
circuit board: 4.49113cm x 2.60809cm
breadboards: 1

parts:
  A1 = d1mini
  R1 = Resistor [tolerance=±5% resistance=330 package=THT]
  R2 = Resistor [tolerance=±5% resistance=10k package=THT]
  J1 = male pin header, 4 pins [form="♂ (male)"]
  S1 = Pushbutton [package="[THT]"]
  Q1 = Basic FET N-Channel [package="TO220 [THT]"]

nets:
  N1: A1.d1, R1.Pin_0
  N2: A1.g, R2.Pin_1, J1.pin3, J1.pin4, S1.Pin_1, S1.Pin_2, Q1.source
  N3: R1.Pin_1, R2.Pin_0, Q1.gate
  N4: J1.pin1, J1.pin2, S1.Pin_3, S1.Pin_4, Q1.drain

notes:
  Garaginator 9,000,000, Garaginator 9,000,000 (CC-BY-SA), B
  GND
  SW
  330Ω
  10KΩ
  GARAGINATOR
  finnie.org
  9,000,000
  2018-10-06
  Rev B
